# Fritzing sketch QoriPunku Esquema (saved by Fritzing 1.0.4)
breadboards: 1

parts:
  LLC1 = Logic Level Converter [package="Breakout board"]  # not connected
  Mod1 = ESP32 - CAM
  Componente1 = Arduino Mega 2560 (Rev3)
  J1 = Basic Servo
  M1 = fc-51 [package=THT]
  HC-SR04_Sensor_1 = HC-SR04 Ultrasonic Distance Sensor
  U1 = RFID RC522 SIP - 8 pins [chip_label="RFID RC522" package="SIP (Single Inline) [THT]"]
  Componente2 = LCD1602-I2C
  Matrix_keypad1 = KEYPAD 4x4
  5V = 4 x AAA Battery Mount [internal_resistance=0.1Ω]  # not connected

nets:
  5V: Mod1.5V, Componente1.5V
  N1: Componente1.A8, J1.pulse
  N2: Componente1.D21/SCL, Componente2.SCL
  N3: Componente1.D20/SDA, Componente2.SDA
  N4: Componente1.D11_PWM, HC-SR04_Sensor_1.TRIG
  N5: Componente1.D10_PWM, HC-SR04_Sensor_1.ECHO
  N6: Componente1.D9_PWM, Matrix_keypad1.row4
  N7: Componente1.D8_PWM, Matrix_keypad1.row3
  3V3: Componente1.3V3, U1.VCC
  GND: Componente1.GND, J1.gnd, M1.pin2, HC-SR04_Sensor_1.GND, U1.GND, Componente2.GND
  N8: Componente1.D2_PWM, Matrix_keypad1.col1
  N9: Componente1.D3_PWM, Matrix_keypad1.col2
  N10: Componente1.D4_PWM, Matrix_keypad1.col3
  N11: Componente1.D5_PWM, Matrix_keypad1.col4
  N12: Componente1.D6_PWM, Matrix_keypad1.row1
  N13: Componente1.D7_PWM, Matrix_keypad1.row2
  N14: Componente1.D22, M1.pin1
  N15: Componente1.D49, U1.RST
  N16: Componente1.D50, U1.MISO
  N17: Componente1.D51, U1.MOSI
  N18: Componente1.D53, U1.NSS
  VCC: J1.vcc, M1.pin3, HC-SR04_Sensor_1.VCC, Componente2.VCC

custom parts:
  Logic Level Converter: 5V to/from 3.3V logic level converter
  ESP32 - CAM: The ESP32-CAM has a very competitive small-size camera module that can operate independently as a minimum system with a footprint of only 27*40.5*4.5mm and a deep sleep current of up to 6mA.
  RFID RC522 SIP - 8 pins: A SIP stand-in part for RFID RC522 . With 8 pins on a 300 mil single inline package (SIP) footprint.
  LCD1602-I2C: A standard character display, usually with 2x16 characters. Comes in many colors with LCM1602 IIC attached.
  KEYPAD 4x4: Matrix keypad 16 buttons, 4 rows x 4 columns
